// Logisim project 1703027.circ as structural Verilog
module SHR (
  input  [2:0] in_1,
  input  [5:0] Input,
  output [5:0] \output 
);

  Multiplexer #(.select(3), .enable("false")) multiplexer_1 (
    .in0(Input[5]), .in1(1'b0), .in2(1'b0), .in3(1'b0), .in4(1'b0), .in5(1'b0), .in6(1'b0), .in7(1'b0),
    .out(\output [5]), .sel(in_1));
  Multiplexer #(.select(3), .enable("false")) multiplexer_2 (
    .in0(Input[4]), .in1(Input[5]), .in2(1'b0), .in3(1'b0), .in4(1'b0), .in5(1'b0), .in6(1'b0), .in7(1'b0),
    .out(\output [4]), .sel(in_1));
  Multiplexer #(.select(3), .enable("false")) multiplexer_3 (
    .in0(Input[3]), .in1(Input[4]), .in2(Input[5]), .in3(1'b0), .in4(1'b0), .in5(1'b0), .in6(1'b0),
    .in7(1'b0), .out(\output [3]), .sel(in_1));
  Multiplexer #(.select(3), .enable("false")) multiplexer_4 (
    .in0(Input[2]), .in1(Input[3]), .in2(Input[4]), .in3(Input[5]), .in4(1'b0), .in5(1'b0), .in6(1'b0),
    .in7(1'b0), .out(\output [2]), .sel(in_1));
  Multiplexer #(.select(3), .enable("false")) multiplexer_5 (
    .in0(Input[1]), .in1(Input[2]), .in2(Input[3]), .in3(Input[4]), .in4(Input[5]), .in5(1'b0), .in6(1'b0),
    .in7(1'b0), .out(\output [1]), .sel(in_1));
  Multiplexer #(.select(3), .enable("false")) multiplexer_6 (
    .in0(Input[0]), .in1(Input[1]), .in2(Input[2]), .in3(Input[3]), .in4(Input[4]), .in5(Input[5]),
    .in6(1'b0), .in7(1'b0), .out(\output [0]), .sel(in_1));

  // Other names for the same wires on the sheet: A0 = Input[0]; A1 = Input[1]; A2 = Input[2]; A3 = Input[3];
  //   A4 = Input[4]; A5 = Input[5]; O0 = \output [0]; O1 = \output [1]; O2 = \output [2]; O3 = \output [3];
  //   O4 = \output [4]; O5 = \output [5]

  // Notes on the sheet:
  //   shift=001 1 bit right shift
  //   shift=010 2 bit right shift
  //   shift
  //   Output
endmodule

module ROL (
  input  [2:0] in_1,
  input  [5:0] in_2,
  output [5:0] out_3
);

  Multiplexer #(.select(3), .enable("false")) multiplexer_1 (
    .in0(in_2[5]), .in1(in_2[4]), .in2(in_2[3]), .in3(in_2[2]), .in4(in_2[1]), .in5(in_2[0]), .in6(1'b0),
    .in7(1'b0), .out(out_3[5]), .sel(in_1));
  Multiplexer #(.select(3), .enable("false")) multiplexer_2 (
    .in0(in_2[4]), .in1(in_2[3]), .in2(in_2[2]), .in3(in_2[1]), .in4(in_2[0]), .in5(in_2[5]), .in6(1'b0),
    .in7(1'b0), .out(out_3[4]), .sel(in_1));
  Multiplexer #(.select(3), .enable("false")) multiplexer_3 (
    .in0(in_2[3]), .in1(in_2[2]), .in2(in_2[1]), .in3(in_2[0]), .in4(in_2[5]), .in5(in_2[4]), .in6(1'b0),
    .in7(1'b0), .out(out_3[3]), .sel(in_1));
  Multiplexer #(.select(3), .enable("false")) multiplexer_4 (
    .in0(in_2[2]), .in1(in_2[1]), .in2(in_2[0]), .in3(in_2[5]), .in4(in_2[4]), .in5(in_2[3]), .in6(1'b0),
    .in7(1'b0), .out(out_3[2]), .sel(in_1));
  Multiplexer #(.select(3), .enable("false")) multiplexer_5 (
    .in0(in_2[1]), .in1(in_2[0]), .in2(in_2[5]), .in3(in_2[4]), .in4(in_2[3]), .in5(in_2[2]), .in6(1'b0),
    .in7(1'b0), .out(out_3[1]), .sel(in_1));
  Multiplexer #(.select(3), .enable("false")) multiplexer_6 (
    .in0(in_2[0]), .in1(in_2[5]), .in2(in_2[4]), .in3(in_2[3]), .in4(in_2[2]), .in5(in_2[1]), .in6(1'b0),
    .in7(1'b0), .out(out_3[0]), .sel(in_1));

  // Other names for the same wires on the sheet: A0 = in_2[0]; A1 = in_2[1]; A2 = in_2[2]; A3 = in_2[3]; A4 = in_2[4];
  //   A5 = in_2[5]; O0 = out_3[0]; O1 = out_3[1]; O2 = out_3[2]; O3 = out_3[3]; O4 = out_3[4]; O5 = out_3[5]

  // Notes on the sheet:
  //   Shift
  //   Input
  //   Output
endmodule

module ALU (
  input  [5:0] in_1,
  input  [5:0] in_2,
  input  op,
  output [5:0] R,
  output SF,
  output CF,
  output ZF
);

  wire or_1_out;
  wire [5:0] rol_1_out_3, shr_1_output;

  SHR shr_1 (.in_1(in_1[2:0]), .\output (shr_1_output), .Input(in_2));
  ROL rol_1 (.in_1(in_1[2:0]), .out_3(rol_1_out_3), .in_2(in_2));
  Multiplexer #(.width(6), .enable("false")) multiplexer_1 (.in0(shr_1_output), .in1(rol_1_out_3), .out(R), .sel(op));
  or or_1 (or_1_out, R[0], R[1], R[2], R[3], R[4], R[5]);
  not not_1 (ZF, or_1_out);

  assign CF = 1'b0;
  assign SF = R[5];

  // Other names for the same wires on the sheet: A[5:0] = in_2; B[5:0] = in_1
endmodule

module _1_bit_register (
  input  Din,
  input  Sel,
  input  Clk,
  output Dout
);

  wire multiplexer_1_out;

  Multiplexer #(.enable("false")) multiplexer_1 (.in0(Dout), .in1(Din), .out(multiplexer_1_out), .sel(Sel));
  D_Flip_Flop d_ff_1 (.clk(Clk), .D(multiplexer_1_out), .Q(Dout));  // open: Qn, preset, en, reset
endmodule

module _6_bit_register (
  input  [5:0] Din_5_0,
  input  Sel,
  input  Clock,
  output [5:0] Dout_5_0
);

  _1_bit_register u_1_bit_register_1 (.Din(Din_5_0[0]), .Sel(Sel), .Clk(Clock), .Dout(Dout_5_0[0]));
  _1_bit_register u_1_bit_register_2 (.Din(Din_5_0[1]), .Sel(Sel), .Clk(Clock), .Dout(Dout_5_0[1]));
  _1_bit_register u_1_bit_register_3 (.Din(Din_5_0[2]), .Sel(Sel), .Clk(Clock), .Dout(Dout_5_0[2]));
  _1_bit_register u_1_bit_register_4 (.Din(Din_5_0[3]), .Sel(Sel), .Clk(Clock), .Dout(Dout_5_0[3]));
  _1_bit_register u_1_bit_register_5 (.Din(Din_5_0[4]), .Sel(Sel), .Clk(Clock), .Dout(Dout_5_0[4]));
  _1_bit_register u_1_bit_register_6 (.Din(Din_5_0[5]), .Sel(Sel), .Clk(Clock), .Dout(Dout_5_0[5]));
endmodule

module Register_set_6_6 (
  input  in_1,
  input  [2:0] Wr,
  input  [5:0] Wrd,
  input  [2:0] Ra,
  input  Clk,
  input  [2:0] Rb,
  output [5:0] A,
  output [5:0] B
);

  wire R0, R1, R2, R3, R4, R5;
  wire [5:0] O0, O1, O2, O3, O4, O5;

  Decoder #(.select(3)) decoder_1 (
    .out0(R0), .out1(R1), .out2(R2), .out3(R3), .out4(R4), .out5(R5), .sel(Wr), .en(in_1));  // open: out6, out7
  _6_bit_register u_6_bit_register_1 (.Din_5_0(Wrd), .Sel(R0), .Clock(Clk), .Dout_5_0(O0));
  _6_bit_register u_6_bit_register_2 (.Din_5_0(Wrd), .Sel(R1), .Clock(Clk), .Dout_5_0(O1));
  _6_bit_register u_6_bit_register_3 (.Din_5_0(Wrd), .Sel(R2), .Clock(Clk), .Dout_5_0(O2));
  _6_bit_register u_6_bit_register_4 (.Din_5_0(Wrd), .Sel(R3), .Clock(Clk), .Dout_5_0(O3));
  _6_bit_register u_6_bit_register_5 (.Din_5_0(Wrd), .Sel(R4), .Clock(Clk), .Dout_5_0(O4));
  _6_bit_register u_6_bit_register_6 (.Din_5_0(Wrd), .Sel(R5), .Clock(Clk), .Dout_5_0(O5));
  Multiplexer #(.select(3), .width(6), .enable("false")) multiplexer_1 (
    .in0(O0), .in1(O1), .in2(O2), .in3(O3), .in4(O4), .in5(O5), .out(A), .sel(Ra));  // open: in6, in7
  Multiplexer #(.select(3), .width(6), .enable("false")) multiplexer_2 (
    .in0(O0), .in1(O1), .in2(O2), .in3(O3), .in4(O4), .in5(O5), .out(B), .sel(Rb));  // open: in6, in7

  // Notes on the sheet:
  //   Reg_enable
endmodule

module _1x1_SRAM (
  input  in_1,
  input  in_2,
  input  in_3,
  input  in_4,
  input  in_5,
  output Read_Data_1,
  output Read_Data_2
);

  wire d_ff_1_q, multiplexer_1_out;

  Multiplexer #(.enable("false")) multiplexer_1 (.in0(d_ff_1_q), .in1(in_3), .out(multiplexer_1_out), .sel(in_4));
  D_Flip_Flop d_ff_1 (.clk(in_5), .D(multiplexer_1_out), .Q(d_ff_1_q));  // open: Qn, preset, en, reset
  and and_1 (Read_Data_1, in_1, d_ff_1_q);
  and and_2 (Read_Data_2, in_2, d_ff_1_q);

  // Notes on the sheet:
  //   Write Data
  //   Write Select
  //   Clock
  //   Read Select 1
  //   Read Select 2
endmodule

module _1x18_SRAM (
  input  [17:0] in_1,
  input  Read_Select_1,
  input  in_3,
  input  in_4,
  input  in_5,
  output [17:0] out_6,
  output [17:0] out_7
);

  _1x1_SRAM u_1x1_sram_1 (
    .in_1(in_3), .in_2(in_4), .in_3(in_1[0]), .in_4(Read_Select_1), .in_5(in_5), .Read_Data_1(out_6[0]),
    .Read_Data_2(out_7[0]));
  _1x1_SRAM u_1x1_sram_2 (
    .in_1(in_3), .in_2(in_4), .in_3(in_1[3]), .in_4(Read_Select_1), .in_5(in_5), .Read_Data_1(out_6[3]),
    .Read_Data_2(out_7[3]));
  _1x1_SRAM u_1x1_sram_3 (
    .in_1(in_3), .in_2(in_4), .in_3(in_1[6]), .in_4(Read_Select_1), .in_5(in_5), .Read_Data_1(out_6[6]),
    .Read_Data_2(out_7[6]));
  _1x1_SRAM u_1x1_sram_4 (
    .in_1(in_3), .in_2(in_4), .in_3(in_1[9]), .in_4(Read_Select_1), .in_5(in_5), .Read_Data_1(out_6[9]),
    .Read_Data_2(out_7[9]));
  _1x1_SRAM u_1x1_sram_5 (
    .in_1(in_3), .in_2(in_4), .in_3(in_1[12]), .in_4(Read_Select_1), .in_5(in_5), .Read_Data_1(out_6[12]),
    .Read_Data_2(out_7[12]));
  _1x1_SRAM u_1x1_sram_6 (
    .in_1(in_3), .in_2(in_4), .in_3(in_1[15]), .in_4(Read_Select_1), .in_5(in_5), .Read_Data_1(out_6[15]),
    .Read_Data_2(out_7[15]));
  _1x1_SRAM u_1x1_sram_7 (
    .in_1(in_3), .in_2(in_4), .in_3(in_1[1]), .in_4(Read_Select_1), .in_5(in_5), .Read_Data_1(out_6[1]),
    .Read_Data_2(out_7[1]));
  _1x1_SRAM u_1x1_sram_8 (
    .in_1(in_3), .in_2(in_4), .in_3(in_1[4]), .in_4(Read_Select_1), .in_5(in_5), .Read_Data_1(out_6[4]),
    .Read_Data_2(out_7[4]));
  _1x1_SRAM u_1x1_sram_9 (
    .in_1(in_3), .in_2(in_4), .in_3(in_1[7]), .in_4(Read_Select_1), .in_5(in_5), .Read_Data_1(out_6[7]),
    .Read_Data_2(out_7[7]));
  _1x1_SRAM u_1x1_sram_10 (
    .in_1(in_3), .in_2(in_4), .in_3(in_1[10]), .in_4(Read_Select_1), .in_5(in_5), .Read_Data_1(out_6[10]),
    .Read_Data_2(out_7[10]));
  _1x1_SRAM u_1x1_sram_11 (
    .in_1(in_3), .in_2(in_4), .in_3(in_1[13]), .in_4(Read_Select_1), .in_5(in_5), .Read_Data_1(out_6[13]),
    .Read_Data_2(out_7[13]));
  _1x1_SRAM u_1x1_sram_12 (
    .in_1(in_3), .in_2(in_4), .in_3(in_1[16]), .in_4(Read_Select_1), .in_5(in_5), .Read_Data_1(out_6[16]),
    .Read_Data_2(out_7[16]));
  _1x1_SRAM u_1x1_sram_13 (
    .in_1(in_3), .in_2(in_4), .in_3(in_1[2]), .in_4(Read_Select_1), .in_5(in_5), .Read_Data_1(out_6[2]),
    .Read_Data_2(out_7[2]));
  _1x1_SRAM u_1x1_sram_14 (
    .in_1(in_3), .in_2(in_4), .in_3(in_1[5]), .in_4(Read_Select_1), .in_5(in_5), .Read_Data_1(out_6[5]),
    .Read_Data_2(out_7[5]));
  _1x1_SRAM u_1x1_sram_15 (
    .in_1(in_3), .in_2(in_4), .in_3(in_1[8]), .in_4(Read_Select_1), .in_5(in_5), .Read_Data_1(out_6[8]),
    .Read_Data_2(out_7[8]));
  _1x1_SRAM u_1x1_sram_16 (
    .in_1(in_3), .in_2(in_4), .in_3(in_1[11]), .in_4(Read_Select_1), .in_5(in_5), .Read_Data_1(out_6[11]),
    .Read_Data_2(out_7[11]));
  _1x1_SRAM u_1x1_sram_17 (
    .in_1(in_3), .in_2(in_4), .in_3(in_1[14]), .in_4(Read_Select_1), .in_5(in_5), .Read_Data_1(out_6[14]),
    .Read_Data_2(out_7[14]));
  _1x1_SRAM u_1x1_sram_18 (
    .in_1(in_3), .in_2(in_4), .in_3(in_1[17]), .in_4(Read_Select_1), .in_5(in_5), .Read_Data_1(out_6[17]),
    .Read_Data_2(out_7[17]));

  // Other names for the same wires on the sheet: Clk = in_5; D0 = in_1[0]; D1 = in_1[1]; D2 = in_1[2]; D3 = in_1[3];
  //   D4 = in_1[4]; D5 = in_1[5]; D6 = in_1[6]; D7 = in_1[7]; D8 = in_1[8]; D9 = in_1[9]; D10 = in_1[10];
  //   D11 = in_1[11]; D12 = in_1[12]; D13 = in_1[13]; D14 = in_1[14]; D15 = in_1[15]; D16 = in_1[16]; D17 = in_1[17];
  //   RD1_0 = out_6[0]; RD1_1 = out_6[1]; RD1_2 = out_6[2]; RD1_3 = out_6[3]; RD1_4 = out_6[4]; RD1_5 = out_6[5];
  //   RD1_6 = out_6[6]; RD1_7 = out_6[7]; RD1_8 = out_6[8]; RD1_9 = out_6[9]; RD1_10 = out_6[10]; RD1_11 = out_6[11];
  //   RD1_12 = out_6[12]; RD1_13 = out_6[13]; RD1_14 = out_6[14]; RD1_15 = out_6[15]; RD1_16 = out_6[16];
  //   RD1_17 = out_6[17]; RD2_0 = out_7[0]; RD2_1 = out_7[1]; RD2_2 = out_7[2]; RD2_3 = out_7[3]; RD2_4 = out_7[4];
  //   RD2_5 = out_7[5]; RD2_6 = out_7[6]; RD2_7 = out_7[7]; RD2_8 = out_7[8]; RD2_9 = out_7[9]; RD2_10 = out_7[10];
  //   RD2_11 = out_7[11]; RD2_12 = out_7[12]; RD2_13 = out_7[13]; RD2_14 = out_7[14]; RD2_15 = out_7[15];
  //   RD2_16 = out_7[16]; RD2_17 = out_7[17]; RS1 = in_3; RS2 = in_4; WS = Read_Select_1

  // Notes on the sheet:
  //   Write Data
  //                       Read Select 2
  //   Clock
  //            Write Select
  //   Read Data 1
  //   Read Data 2
endmodule

module Sram_Test (
  input  [17:0] in_1,
  input  in_2,
  input  in_3,
  input  in_4,
  input  in_5,
  output [17:0] out_6,
  output [17:0] out_7
);

  _1x18_SRAM u_1x18_sram_1 (
    .in_1(in_1), .Read_Select_1(in_4), .in_3(in_2), .in_4(in_3), .in_5(in_5), .out_6(out_6), .out_7(out_7));

  // Notes on the sheet:
  //   Write Data
  //   Read Data 1
  //   Read Data 2
endmodule

module _9x18_SRAM (
  input  [17:0] in_1,
  input  in_2,
  input  [3:0] in_3,
  input  [3:0] in_4,
  input  [3:0] in_5,
  input  Clock,
  output [17:0] out_7,
  output [17:0] out_8
);

  wire R1_0, R1_1, R1_2, R1_3, R1_4, R1_5, R1_6, R1_7, R1_8, R2_0, R2_1, R2_2, R2_3, R2_4, R2_5, R2_6, R2_7,
       R2_8, W0, W1, W2, W3, W4, W5, W6, W7, W8;
  wire [17:0] RD1_0, RD1_1, RD1_2, RD1_3, RD1_4, RD1_5, RD1_6, RD1_7, RD1_8, RD2_0, RD2_1, RD2_2, RD2_3,
       RD2_4, RD2_5, RD2_6, RD2_7, RD2_8;

  Decoder #(.select(4)) decoder_1 (
    .out0(W0), .out1(W1), .out2(W2), .out3(W3), .out4(W4), .out5(W5), .out6(W6), .out7(W7), .out8(W8),
    .sel(in_3), .en(in_2));  // open: out9, out10, out11, out12, out13, out14, out15
  Decoder #(.select(4), .enable("false")) decoder_2 (
    .out0(R2_0), .out1(R2_1), .out2(R2_2), .out3(R2_3), .out4(R2_4), .out5(R2_5), .out6(R2_6), .out7(R2_7),
    .out8(R2_8), .sel(in_5));  // open: out9, out10, out11, out12, out13, out14, out15
  Decoder #(.select(4), .enable("false")) decoder_3 (
    .out0(R1_0), .out1(R1_1), .out2(R1_2), .out3(R1_3), .out4(R1_4), .out5(R1_5), .out6(R1_6), .out7(R1_7),
    .out8(R1_8), .sel(in_4));  // open: out9, out10, out11, out12, out13, out14, out15
  _1x18_SRAM u_1x18_sram_1 (
    .in_1(in_1), .Read_Select_1(W0), .in_3(R1_0), .in_4(R2_0), .in_5(Clock), .out_6(RD1_0), .out_7(RD2_0));
  _1x18_SRAM u_1x18_sram_2 (
    .in_1(in_1), .Read_Select_1(W1), .in_3(R1_1), .in_4(R2_1), .in_5(Clock), .out_6(RD1_1), .out_7(RD2_1));
  _1x18_SRAM u_1x18_sram_3 (
    .in_1(in_1), .Read_Select_1(W2), .in_3(R1_2), .in_4(R2_2), .in_5(Clock), .out_6(RD1_2), .out_7(RD2_2));
  _1x18_SRAM u_1x18_sram_4 (
    .in_1(in_1), .Read_Select_1(W3), .in_3(R1_3), .in_4(R2_3), .in_5(Clock), .out_6(RD1_3), .out_7(RD2_3));
  _1x18_SRAM u_1x18_sram_5 (
    .in_1(in_1), .Read_Select_1(W4), .in_3(R1_4), .in_4(R2_4), .in_5(Clock), .out_6(RD1_4), .out_7(RD2_4));
  _1x18_SRAM u_1x18_sram_6 (
    .in_1(in_1), .Read_Select_1(W5), .in_3(R1_5), .in_4(R2_5), .in_5(Clock), .out_6(RD1_5), .out_7(RD2_5));
  _1x18_SRAM u_1x18_sram_7 (
    .in_1(in_1), .Read_Select_1(W6), .in_3(R1_6), .in_4(R2_6), .in_5(Clock), .out_6(RD1_6), .out_7(RD2_6));
  _1x18_SRAM u_1x18_sram_8 (
    .Read_Select_1(W7), .in_3(R1_7), .in_4(R2_7), .in_5(Clock), .out_6(RD1_7), .out_7(RD2_7));  // open: in_1
  _1x18_SRAM u_1x18_sram_9 (
    .in_1(in_1), .Read_Select_1(W8), .in_3(R1_8), .in_4(R2_8), .in_5(Clock), .out_6(RD1_8), .out_7(RD2_8));
  assign out_7 = RD1_0 | RD1_1 | RD1_2 | RD1_3 | RD1_4 | RD1_5 | RD1_6 | RD1_7 | RD1_8;  // OR_Gate or_1, 18 bits wide
  assign out_8 = RD2_0 | RD2_1 | RD2_2 | RD2_3 | RD2_4 | RD2_5 | RD2_6 | RD2_7 | RD2_8;  // OR_Gate or_2, 18 bits wide

  // Notes on the sheet:
  //           Write enable
  //   Write Data [17:0]
  //   Write address[3:0]
  //   Read Address 2 [3:0]
  //   Read Address 1 [3:0]
  //   Read Data 1
  //   Read Data 2[17:0]
endmodule

module _4_bit_counter_register (
  input  [3:0] Din_3_0,
  input  Clock,
  output [3:0] Dout_3_0
);

  _1_bit_register u_1_bit_register_1 (.Din(Din_3_0[0]), .Sel(1'b1), .Clk(Clock), .Dout(Dout_3_0[0]));
  _1_bit_register u_1_bit_register_2 (.Din(Din_3_0[1]), .Sel(1'b1), .Clk(Clock), .Dout(Dout_3_0[1]));
  _1_bit_register u_1_bit_register_3 (.Din(Din_3_0[2]), .Sel(1'b1), .Clk(Clock), .Dout(Dout_3_0[2]));
  _1_bit_register u_1_bit_register_4 (.Din(Din_3_0[3]), .Sel(1'b1), .Clk(Clock), .Dout(Dout_3_0[3]));
endmodule

module CPU (
  input  [17:0] in_1,
  input  [3:0] in_2,
  input  in_3,
  input  Clock,
  input  CPU_Enable
);

  wire alu_1_cf, alu_1_sf, alu_1_zf, CPU_CLK, Imm_Sel, Jmp_Sel, Op, We, ZF;
  wire [3:0] Jmp_Addr, multiplexer_1_out, n4_bit_counter_register_1_dout_3_0, n4_bit_pc_adder_1_o_3_0;
  wire [5:0] alu_1_r, multiplexer_2_out, register_set_6_6_1_a, register_set_6_6_1_b;
  wire [17:0] n9x18_sram_1_out_7;

  Multiplexer #(.width(4), .disabled(0), .enable("false")) multiplexer_1 (
    .in0(n4_bit_pc_adder_1_o_3_0), .in1(Jmp_Addr), .out(multiplexer_1_out), .sel(Jmp_Sel));
  _4_bit_pc_adder u_4_bit_pc_adder_1 (.I__3_0(n4_bit_counter_register_1_dout_3_0), .O_3_0(n4_bit_pc_adder_1_o_3_0));
  and and_1 (CPU_CLK, Clock, CPU_Enable);
  _4_bit_counter_register u_4_bit_counter_register_1 (
    .Din_3_0(multiplexer_1_out), .Clock(CPU_CLK), .Dout_3_0(n4_bit_counter_register_1_dout_3_0));
  _9x18_SRAM u_9x18_sram_1 (
    .in_1(in_1), .in_2(in_3), .in_3(in_2), .in_4(n4_bit_counter_register_1_dout_3_0), .Clock(Clock),
    .out_7({n9x18_sram_1_out_7[17:15], Jmp_Addr, n9x18_sram_1_out_7[10:0]}));  // open: in_5, out_8
  Register_set_6_6 register_set_6_6_1 (
    .in_1(We), .Wr(Jmp_Addr[3:1]), .Wrd(alu_1_r), .Ra(Jmp_Addr[3:1]), .Clk(CPU_CLK),
    .Rb({Jmp_Addr[0], n9x18_sram_1_out_7[10:9]}), .A(register_set_6_6_1_a), .B(register_set_6_6_1_b));
  Flag_Register flag_register_1 (
    .ZFin(alu_1_zf), .CFin(alu_1_cf), .SFin(alu_1_sf), .CLock(CPU_CLK), .ZFout(ZF));  // open: CFout, SFout
  ALU alu_1 (
    .in_1(multiplexer_2_out), .in_2(register_set_6_6_1_a), .op(Op), .R(alu_1_r), .SF(alu_1_sf),
    .CF(alu_1_cf), .ZF(alu_1_zf));
  Multiplexer #(.width(6), .disabled(0), .enable("false")) multiplexer_2 (
    .in0(register_set_6_6_1_b), .in1({Jmp_Addr[0], n9x18_sram_1_out_7[10:6]}), .out(multiplexer_2_out),
    .sel(Imm_Sel));
  Control_Unit control_unit_1 (
    .Opcode_2_0(n9x18_sram_1_out_7[17:15]), .ZF(ZF), .OP(Op), .Imm_Sel(Imm_Sel), .WE(We), .Jmp_Sel(Jmp_Sel));

  // Other names for the same wires on the sheet: CLK = Clock

  // Notes on the sheet:
  //   Write Data [17:0]
  //   Write address[3:0]
  //           Write enable
  //   Register Mode: Opcode(2+1) bit+Register Ra(3bit)+Register Rb(3 bit) +Unused(9bit)
  //   Branching Mode: Opcode(2+1) bit+Address(4 bit) +Unused(11 bit)
  //   Immediate Mode: Opcode(2+1) bit+Register Ra(3bit)+Immediate Value(6bit) +Unused(6 bit)
endmodule

module _4_bit_pc_adder (
  input  [3:0] I__3_0,
  output [3:0] O_3_0
);

  wire [3:0] bit_extender_1_out;

  assign bit_extender_1_out = {{3{1'b0}}, 1'b1};  // Bit_Extender bit_extender_1
  Adder #(.width(4)) adder_1 (.a(I__3_0), .b(bit_extender_1_out), .out(O_3_0));  // open: cin, cout
endmodule

module adder_test (
  input  [3:0] in_1,
  output [3:0] out_2
);

  _4_bit_pc_adder u_4_bit_pc_adder_1 (.I__3_0(in_1), .O_3_0(out_2));
endmodule

module Flag_Register (
  input  ZFin,
  input  CFin,
  input  SFin,
  input  CLock,
  output ZFout,
  output CFout,
  output SFout
);

  _1_bit_register u_1_bit_register_1 (.Din(ZFin), .Sel(1'b1), .Clk(CLock), .Dout(ZFout));
  _1_bit_register u_1_bit_register_2 (.Din(CFin), .Sel(1'b1), .Clk(CLock), .Dout(CFout));
  _1_bit_register u_1_bit_register_3 (.Din(SFin), .Sel(1'b1), .Clk(CLock), .Dout(SFout));
endmodule

module Control_Unit (
  input  [2:0] Opcode_2_0,
  input  ZF,
  output OP,
  output Imm_Sel,
  output WE,
  output Jmp_Sel
);

  wire and_1_out, Branch_out, not_1_out, not_2_out, not_3_out, not_4_out, not_5_out, not_6_out, WE_out;

  not not_1 (not_1_out, Opcode_2_0[1]);
  not not_2 (not_2_out, Opcode_2_0[2]);
  not not_3 (not_3_out, Opcode_2_0[1]);
  not not_4 (not_4_out, Opcode_2_0[2]);
  buf u_WE (WE_out, not_1_out);  // AND_Gate
  and Branch (Branch_out, Opcode_2_0[2], not_3_out);
  not not_5 (not_5_out, Opcode_2_0[0]);
  not not_6 (not_6_out, ZF);
  buf IMM (Imm_Sel, Opcode_2_0[1]);  // AND_Gate
  and and_1 (and_1_out, not_5_out, not_6_out);
  or or_1 (WE, Imm_Sel, WE_out);
  and JNZ (Jmp_Sel, Branch_out, and_1_out);

  assign OP = Opcode_2_0[0];
endmodule
